# Fritzing sketch fritzing (saved by Fritzing 0.9.4)
breadboards: 3

parts:
  DHT1 = DHT22 Humidity and Temperature Sensor
  U1 = NodeMCU V3.0
  PIR1 = PIR sensor
  U2 = NodeMCU V3.0
  PIR2 = PIR sensor
  R1 = Resistor [tolerance=±5% resistance=100 package="0603 [SMD]"]
  R2 = Resistor [tolerance=±5% resistance=100 package="0603 [SMD]"]
  U3 = NodeMCU V3.0
  R3 = PHOTOCELL [package=photocell-kit]
  R4 = Resistor [tolerance=±5% resistance=10k package="0603 [SMD]"]
  LED1 = LEDs [package=led10mm]
  R5 = Resistor [tolerance=±5% resistance=220 package="0603 [SMD]"]
  M5StickC1 = M5StickC  # not connected

nets:
  VDD: DHT1.VDD, U1.3V3
  N1: DHT1.DATA, U1.D2
  N2: DHT1.GND, U1.GND#6, U1.GND#13, U1.GND#16, U1.GND#33
  VDD_2: PIR1.VDD, U2.3V3, PIR2.VDD
  N3: PIR1.SIG, U2.D3
  N4: PIR1.GND, R2.Pin_1
  N5: U2.D4, PIR2.SIG
  N6: U2.GND#6, U2.GND#13, U2.GND#16, U2.GND#33, R1.Pin_0, R2.Pin_0
  N7: PIR2.GND, R1.Pin_1
  N8: U3.D2, LED1.A
  N9: U3.3V3, R3.P$1, R5.Pin_0
  N10: U3.GND#6, U3.GND#13, U3.GND#16, U3.GND#33, R4.Pin_1
  N11: U3.A0, R3.P$2, R4.Pin_0
  N12: LED1.C, R5.Pin_1

notes:
  display
  personCounter
  collector
  handler

custom parts:
  NodeMCU V3.0: ESP8266 based NodeMCU
