# Fritzing sketch fritzing (saved by Fritzing 0.9.4)
breadboards: 2

parts:
  DHT1 = DHT22 Humidity and Temperature Sensor
  U1 = NodeMCU V3.0
  PIR1 = PIR sensor
  U2 = NodeMCU V3.0

nets:
  VDD: DHT1.VDD, U1.3V3
  N1: DHT1.DATA, U1.D2
  N2: DHT1.GND, U1.GND#6, U1.GND#13, U1.GND#16, U1.GND#33
  VDD_2: PIR1.VDD, U2.3V3
  N3: PIR1.GND, U2.GND#6, U2.GND#13, U2.GND#16, U2.GND#33

custom parts:
  NodeMCU V3.0: ESP8266 based NodeMCU
